# Fritzing sketch JP_Oracle_FountainV1 (saved by Fritzing 1.0.0rc)
breadboards: 1

parts:
  A1 = Particle - Photon2
  Relay1 = Relay - 6 pins [package="DIP (Dual Inline) [THT]"]
  R1 = Resistor [tolerance=±5% power=0.25W resistance=220 package=THT]
  Q1 = PNP-Transistor [package="TO92 [THT]"]
  R2 = Resistor [tolerance=±5% power=0.25W resistance=220 package=THT]
  M2 = DC Motor [voltage_(max)=6V voltage_(min)=3V]
  J1 = Screw terminal - 2 pins [package=THT]
  M3 = BMP280
  Part1 = Adafruit VL530X Time of Flight Distance Sensor [part_number="Adafruit #3317"]
  DFRobot_DFPlayer_Mini1 = DFRobot DFPlayer Mini [part_number=DFR0299]
  SP1 = SPEAKER [package=pcb_mount_speaker]
  Neopixel1 = Adafruit RBG Smart Neopixel [package="DIP (Dual Inline) [THT]"]
  S1 = Square Pushbutton
  Part2 = 12 NeoPixel Ring [part_number=1643]
  TTP223B1 = TTP223B Capacitive Touch Sensor Module
  Neopixel2 = Adafruit RBG Smart Neopixel [package="DIP (Dual Inline) [THT]"]
  Neopixel3 = Adafruit RBG Smart Neopixel [package="DIP (Dual Inline) [THT]"]
  Neopixel4 = Adafruit RBG Smart Neopixel [package="DIP (Dual Inline) [THT]"]
  Neopixel5 = Adafruit RBG Smart Neopixel [package="DIP (Dual Inline) [THT]"]

nets:
  N1: A1.Pin_1, A1.Pin_40, S1.leg1
  VCC: A1.Pin_2, A1.Pin_31, Relay1.VCC, M3.VIN, Part1.VCC, DFRobot_DFPlayer_Mini1.VCC, TTP223B1.VCC
  GND: A1.Pin_4, A1.Pin_30, A1.Pin_32, Relay1.GND, Q1.C, R2.Pin_0, M3.GND, Part1.GND, DFRobot_DFPlayer_Mini1.GND-1, DFRobot_DFPlayer_Mini1.GND-2, Neopixel1.G, S1.leg0, Part2.GND, TTP223B1.GND, Neopixel2.G, Neopixel3.G, Neopixel4.G, Neopixel5.G
  N2: A1.Pin_12, Part2.IN
  N3: A1.Pin_14, DFRobot_DFPlayer_Mini1.TX
  N4: A1.Pin_15, DFRobot_DFPlayer_Mini1.RX
  N5: A1.Pin_17, M3.SDA, Part1.SDA
  N6: A1.Pin_19, Neopixel1.In
  N7: A1.Pin_20, TTP223B1.SIG
  N8: A1.Pin_24, Q1.B, R2.Pin_1
  N9: A1.Pin_26, R1.Pin_0, Neopixel1.+, Part2.VDD, Neopixel2.+, Neopixel3.+, Neopixel4.+, Neopixel5.+
  N10: Relay1.IN, R1.Pin_1, Q1.E
  N11: Relay1.COM, M2.pin_1
  N12: Relay1.ON, J1.pin2
  N13: M2.pin_2, J1.pin1
  N14: M3.SCL, Part1.SCL
  N15: DFRobot_DFPlayer_Mini1.SPK_1, SP1.-
  N16: DFRobot_DFPlayer_Mini1.SPK_2, SP1.+
  N17: Neopixel1.O, Neopixel2.In
  N18: Neopixel2.O, Neopixel3.In
  N19: Neopixel3.O, Neopixel4.In
  N20: Neopixel4.O, Neopixel5.In

custom parts:
  Particle - Photon2: The Photon 2 is a microcontroller and Wi-Fi networking developed by particle. Features: 802.11a/b/g/n Wi-Fi, 2.4 GHz and 5 GHz Integrated PCB antenna Integrated U.FL connector for external antenna Integrated RF switch BLE 5 using same antenna as Wi-Fi Realtek RTL8721DM MCU ARM Cortex M33 CPU, 200 MHz 2048 KB (2 MB) user application maximum size 3072 KB (3 MB) of RAM available to user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
  Relay - 6 pins: A DIP stand-in part for whatever IC you want. With 6 pins on a 900mil dual inline package (DIP) footprint.
  BMP280: Temperature Humidity Barometric presure Sensor, I2C
  Adafruit VL530X Time of Flight Distance Sensor: The VL53L0X is a Time of Flight distance sensor like no other you've used! The sensor contains a very tiny invisible laser source, and a matching sensor. The VL53L0X can detect the "time of flight", or how long the light has taken to bounce back to the sensor. Since it uses a very narrow light source, it is good for determining distance of only the surface directly in front of it. Unlike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
  12 NeoPixel Ring: 12 ultra bright smart LED NeoPixels are arranged in a circle with 1.5" (37mm) outer diameter. The rings are 'chainable' - connect the output pin of one to the input pin of another. Use only one microcontroller pin to control as many as you can chain together! Each LED is addressable as the driver chip is inside the LED. Each one has ~18mA constant current drive so the color will be very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
  TTP223B Capacitive Touch Sensor Module: The TTP223B capacitive touch sensor module uses the TTP223B IC. The appropriate voltage is approximately 2 to 5.5 volts.
